// Logisim project codebook.circ as structural Verilog: 7 circuits, main circuit main
module main (
);
endmodule

module half_adder (
  input  A_in,
  input  B_in,
  output Sum_out,
  output Carry_out
);

  xor xor_1 (Sum_out, A_in, B_in);
  and and_1 (Carry_out, A_in, B_in);
endmodule

module full_adder (
  input  Carry_in,
  input  A_in,
  input  B_in,
  output Sum_out,
  output Carry_out
);

  wire half_adder_1_carry_out, half_adder_2_carry_out, half_adder_2_sum_out;

  half_adder half_adder_1 (
    .A_in(Carry_in), .B_in(half_adder_2_sum_out), .Sum_out(Sum_out), .Carry_out(half_adder_1_carry_out));
  half_adder half_adder_2 (
    .A_in(A_in), .B_in(B_in), .Sum_out(half_adder_2_sum_out), .Carry_out(half_adder_2_carry_out));
  or or_1 (Carry_out, half_adder_1_carry_out, half_adder_2_carry_out);
endmodule

module _8_bit_adder (
  input  Carry_in,
  input  A0,
  input  B0,
  input  A1,
  input  B1,
  input  A2,
  input  B2,
  input  A3,
  input  B3,
  input  A4,
  input  B4,
  input  A5,
  input  B5,
  input  A6,
  input  B6,
  input  A7,
  input  B7,
  output S0,
  output S1,
  output S2,
  output S3,
  output S4,
  output S5,
  output S6,
  output S7,
  output Carry_out
);

  wire full_adder_1_carry_out, full_adder_2_carry_out, full_adder_3_carry_out, full_adder_4_carry_out,
       full_adder_5_carry_out, full_adder_6_carry_out, full_adder_7_carry_out;

  full_adder full_adder_1 (.Carry_in(Carry_in), .A_in(A0), .B_in(B0), .Sum_out(S0), .Carry_out(full_adder_1_carry_out));
  full_adder full_adder_2 (
    .Carry_in(full_adder_1_carry_out), .A_in(A1), .B_in(B1), .Sum_out(S1), .Carry_out(full_adder_2_carry_out));
  full_adder full_adder_3 (
    .Carry_in(full_adder_2_carry_out), .A_in(A2), .B_in(B2), .Sum_out(S2), .Carry_out(full_adder_3_carry_out));
  full_adder full_adder_4 (
    .Carry_in(full_adder_3_carry_out), .A_in(A3), .B_in(B3), .Sum_out(S3), .Carry_out(full_adder_4_carry_out));
  full_adder full_adder_5 (
    .Carry_in(full_adder_4_carry_out), .A_in(A4), .B_in(B4), .Sum_out(S4), .Carry_out(full_adder_5_carry_out));
  full_adder full_adder_6 (
    .Carry_in(full_adder_5_carry_out), .A_in(A5), .B_in(B5), .Sum_out(S5), .Carry_out(full_adder_6_carry_out));
  full_adder full_adder_7 (
    .Carry_in(full_adder_6_carry_out), .A_in(A6), .B_in(B6), .Sum_out(S6), .Carry_out(full_adder_7_carry_out));
  full_adder full_adder_8 (
    .Carry_in(full_adder_7_carry_out), .A_in(A7), .B_in(B7), .Sum_out(S7), .Carry_out(Carry_out));
endmodule

module ones_complement (
  input  In,
  input  in_2,
  input  in_3,
  input  in_4,
  input  in_5,
  input  in_6,
  input  in_7,
  input  in_8,
  input  Negate,
  output Out,
  output out_11,
  output out_12,
  output out_13,
  output out_14,
  output out_15,
  output out_16,
  output out_17
);

  xor xor_1 (Out, In, Negate);
  xor xor_2 (out_11, in_2, Negate);
  xor xor_3 (out_12, in_3, Negate);
  xor xor_4 (out_13, in_4, Negate);
  xor xor_5 (out_14, in_5, Negate);
  xor xor_6 (out_15, in_6, Negate);
  xor xor_7 (out_16, in_7, Negate);
  xor xor_8 (out_17, in_8, Negate);
endmodule

module subadder (
  input  SUB,
  input  in_2,
  input  in_3,
  input  in_4,
  input  in_5,
  input  in_6,
  input  in_7,
  input  in_8,
  input  in_9,
  input  in_10,
  input  in_11,
  input  in_12,
  input  in_13,
  input  in_14,
  input  in_15,
  input  in_16,
  input  in_17,
  output out_18,
  output out_19,
  output out_20,
  output out_21,
  output out_22,
  output out_23,
  output out_24,
  output out_25,
  output Overflow_underflow
);

  wire n8_bit_adder_1_carry_out, ones_complement_1_out, ones_complement_1_out_11, ones_complement_1_out_12,
       ones_complement_1_out_13, ones_complement_1_out_14, ones_complement_1_out_15,
       ones_complement_1_out_16, ones_complement_1_out_17;

  xor xor_1 (Overflow_underflow, SUB, n8_bit_adder_1_carry_out);
  _8_bit_adder u_8_bit_adder_1 (
    .A0(in_10), .B0(ones_complement_1_out), .A1(in_11), .B1(ones_complement_1_out_11), .A2(in_12),
    .B2(ones_complement_1_out_12), .A3(in_13), .B3(ones_complement_1_out_13), .A4(in_14),
    .B4(ones_complement_1_out_14), .A5(in_15), .B5(ones_complement_1_out_15), .A6(in_16),
    .B6(ones_complement_1_out_16), .A7(in_17), .B7(ones_complement_1_out_17), .Carry_in(SUB),
    .Carry_out(n8_bit_adder_1_carry_out), .S0(out_21), .S1(out_25), .S2(out_20), .S3(out_24), .S4(out_19),
    .S5(out_23), .S6(out_18), .S7(out_22));
  ones_complement ones_complement_1 (
    .In(in_5), .in_2(in_9), .in_3(in_4), .in_4(in_8), .in_5(in_3), .in_6(in_7), .in_7(in_2), .in_8(in_6),
    .Negate(SUB), .Out(ones_complement_1_out), .out_11(ones_complement_1_out_11),
    .out_12(ones_complement_1_out_12), .out_13(ones_complement_1_out_13), .out_14(ones_complement_1_out_14),
    .out_15(ones_complement_1_out_15), .out_16(ones_complement_1_out_16), .out_17(ones_complement_1_out_17));
endmodule

module RS_flip_flop (
  input  R,
  input  S,
  output Q,
  output Qbar
);

  nor nor_1 (Q, R, Qbar);
  nor nor_2 (Qbar, Q, S);
endmodule
